# Fritzing sketch ratpack_wifly (saved by Fritzing 0.7.10b)
breadboards: 1

parts:
  Sparkfun_Wifly_Shield_on_top_of_Arduino_Uno = Arduino WiFly Shield
  LED = LED - 5mm [color="Green (565nm)" package="5 mm [THT]"]
  R2_220_Ω = Resistor [tolerance=±5% resistance=220 package=THT]
  Switch = Pushbutton [package=THT]
  R1_10_kΩ = Resistor [tolerance=±5% resistance=10k package=THT]

nets:
  N1: Sparkfun_Wifly_Shield_on_top_of_Arduino_Uno.5V, Switch.leg0, R1_10_kΩ.Pin_0
  N2: Sparkfun_Wifly_Shield_on_top_of_Arduino_Uno.D2, Switch.leg1, R1_10_kΩ.Pin_1
  N3: Sparkfun_Wifly_Shield_on_top_of_Arduino_Uno.D9, R2_220_Ω.Pin_0
  N4: Sparkfun_Wifly_Shield_on_top_of_Arduino_Uno.GND, LED.cathode
  N5: LED.anode, R2_220_Ω.Pin_1

notes:
  rat pack kit
  makingthingshappen.de
  CC BY-SA 3.0
  Find all sources:
  github.com/5v3n/ratpack
